# Fritzing sketch pikvm-final (saved by Fritzing 0.9.3b)
perfboards: 2
breadboards: 1

parts:
  Arduino_Pro_micro = Arduino Pro Micro (Clone)
  Level_Shifter = Logic Level Converter
  Q1 = TRANSISTOR_NPN [package=to-92]
  Raspberry_Pi_1 = Raspberry Pi 3 [part_number=RPI-3-V1.2]
  J1 = Screw terminal - 2 pins [package=THT]
  J2 = female pin header, 2 pins [form="♀ (female)"]
  J3 = Screw terminal - 2 pins [package=THT]
  J4 = Screw terminal - 2 pins [package=THT]
  J5 = Screw terminal - 2 pins [package=THT]
  J6 = female pin header, 2 pins [form="♀ (female)"]
  J7 = female pin header, 2 pins [form="♀ (female)"]
  J8 = female pin header, 2 pins [form="♀ (female)"]
  R1 = Resistor [tolerance=±5% resistance=470 package="0805 [SMD]"]
  R2 = Resistor [tolerance=±5% resistance=470 package="0805 [SMD]"]
  R3 = Resistor [tolerance=±5% resistance=470 package="0805 [SMD]"]
  R4 = Resistor [tolerance=±5% resistance=4.7k package="0805 [SMD]"]
  R5 = Resistor [tolerance=±5% resistance=4.7k package="0805 [SMD]"]
  R6 = Resistor [tolerance=±5% resistance=470 package="0805 [SMD]"]
  R7 = Resistor [tolerance=±5% resistance=470 package="0805 [SMD]"]
  J32 = female pin header, 2 pins [form="♀ (female)"]  # not connected
  J33 = female pin header, 2 pins [form="♀ (female)"]  # not connected
  J34 = female pin header, 2 pins [form="♀ (female)"]  # not connected
  Raspberry_Pi_4 = Raspberry Pi 3 [part_number=RPI-3-V1.2]
  R16 = Resistor [tolerance=±5% resistance=470 package="0805 [SMD]"]
  Arduino_Pro_micro2 = Arduino Pro Micro (Clone)
  IC1 = IC, DIP package, 4 pins [chip_label=IC]
  IC2 = IC, DIP package, 4 pins [chip_label=IC]
  IC3 = IC, DIP package, 4 pins [chip_label=IC]
  IC4 = IC, DIP package, 4 pins [chip_label=IC]
  IC5 = IC, DIP package, 4 pins [chip_label=IC]
  R15 = Resistor [tolerance=±5% resistance=470 package="0805 [SMD]"]
  IC6 = IC, DIP package, 4 pins [chip_label=IC]
  IC7 = IC, DIP package, 4 pins [chip_label=IC]
  IC8 = IC, DIP package, 4 pins [chip_label=IC]
  R18 = Resistor [tolerance=±5% resistance=4.7k package="0805 [SMD]"]
  R19 = Resistor [tolerance=±5% resistance=4.7k package="0805 [SMD]"]
  R20 = Resistor [tolerance=±5% resistance=470 package="0805 [SMD]"]
  R21 = Resistor [tolerance=±5% resistance=470 package="0805 [SMD]"]
  J31 = female pin header, 2 pins [form="♀ (female)"]
  J38 = male pin header, 8 pins [form="♂ (male)"]
  Level_Shifter3 = Logic Level Converter
  Q3 = TRANSISTOR_NPN [package=to-92]
  R22 = Resistor [tolerance=±5% resistance=470 package="0805 [SMD]"]
  J37 = shrouded pin header, 20 pins [form="♂ (shrouded male)"]

nets:
  N1: Arduino_Pro_micro.TXO, Level_Shifter.RX2_HV
  N2: Arduino_Pro_micro.RXI, Level_Shifter.TX2_HV
  GND: Arduino_Pro_micro.GND, Level_Shifter.GND, Q1.E, Raspberry_Pi_1.GND, R2.Pin_0, R3.Pin_0, R4.Pin_1, R5.Pin_1
  VCC: Arduino_Pro_micro.VCC, Level_Shifter.HV, Raspberry_Pi_1.5V
  N3: Arduino_Pro_micro.RST, Q1.C
  N4: Level_Shifter.TX2_LV, Raspberry_Pi_1.GIPO14
  N5: Level_Shifter.RX2_LV, Raspberry_Pi_1.GIPO15
  3V3: Level_Shifter.LV, Raspberry_Pi_1.3v3, Raspberry_Pi_1.3V3, Raspberry_Pi_1.GIPO23, IC1.pin4, IC2.pin4, IC4.pin1
  N6: Q1.B, R1.Pin_1
  N7: Raspberry_Pi_1.GIPO4, R1.Pin_0
  N8: Raspberry_Pi_1.GIPO27, IC3.pin1
  N9: Raspberry_Pi_1.GIPO22, R4.Pin_0, IC1.pin3
  N10: Raspberry_Pi_1.GIPO24, R5.Pin_0, IC2.pin3
  N11: J1.pin1, J7.pin1, IC2.pin2
  N12: J1.pin2, J7.pin2, R6.Pin_0
  N13: J2.pin1, J5.pin1, IC4.pin3, J31.pin2
  N14: J2.pin2, J5.pin2, IC4.pin4
  N15: J3.pin1, J8.pin1, IC1.pin2
  N16: J3.pin2, J8.pin2, R7.Pin_0
  N17: J4.pin1, J6.pin1, IC3.pin3
  N18: J4.pin2, J6.pin2, IC3.pin4
  N19: R2.Pin_1, IC4.pin2
  N20: R3.Pin_1, IC3.pin2
  N21: R6.Pin_1, IC2.pin1
  N22: R7.Pin_1, IC1.pin1
  3V3_2: Raspberry_Pi_4.3v3, Raspberry_Pi_4.GPIO2, Raspberry_Pi_4.GPIO3, Raspberry_Pi_4.5V, Arduino_Pro_micro2.VCC, IC5.pin4, IC6.pin4, Level_Shifter3.LV, Level_Shifter3.HV
  N23: Raspberry_Pi_4.GIPO4, R22.Pin_0
  GND_2: Raspberry_Pi_4.GND, Raspberry_Pi_4.GIPO27, Raspberry_Pi_4.GIPO14, Arduino_Pro_micro2.GND, IC7.pin1, R18.Pin_1, R19.Pin_1, R20.Pin_0, R21.Pin_0, Level_Shifter3.TX2_LV, Level_Shifter3.GND, Q3.E
  N24: Raspberry_Pi_4.GIPO22, IC5.pin3, R18.Pin_0
  N25: Raspberry_Pi_4.GIPO24, IC6.pin3, R19.Pin_0
  N26: Raspberry_Pi_4.GIPO23, IC8.pin1
  N27: Raspberry_Pi_4.GIPO15, Level_Shifter3.RX2_LV
  N28: R16.Pin_0, J38.pin4, J37.pin20
  N29: R16.Pin_1, IC6.pin1
  N30: Arduino_Pro_micro2.TXO, Level_Shifter3.RX2_HV
  N31: Arduino_Pro_micro2.RXI, Level_Shifter3.TX2_HV
  N32: Arduino_Pro_micro2.RST, Q3.C
  N33: IC5.pin1, R15.Pin_1
  N34: IC5.pin2, J38.pin1, J37.pin2
  N35: R15.Pin_0, J38.pin2, J37.pin1
  N36: IC6.pin2, J38.pin3, J37.pin19
  N37: IC7.pin2, R21.Pin_1
  N38: IC7.pin3, J38.pin5, J37.pin3
  N39: IC7.pin4, J38.pin6, J37.pin4
  N40: IC8.pin2, R20.Pin_1
  N41: IC8.pin3, J38.pin7, J37.pin17
  N42: IC8.pin4, J38.pin8, J37.pin18
  N43: Q3.B, R22.Pin_1

notes:
  HDD LED
  POWER LED
  RESET SW
  POWER SW
  Motherboard
  Arduino to USB PC
  HDMI CSI to PC
